# Fritzing sketch tmp_servo (saved by Fritzing 0.9.3b)
breadboards: 1

parts:
  Part1 = Photon
  U1 = TMP36 [package=to-92]
  J1 = Basic Servo

nets:
  N1: Part1.A0, U1.VOUT
  GND: Part1.GND, U1.GND, J1.gnd
  VIN: Part1.VIN, J1.vcc
  N2: Part1.D0, J1.pulse
  3V3: Part1.3V3, U1.VCC

notes:
  3.3VDC
  4.8VDC
